# Fritzing sketch diagram_circuit_tfg_v2 (saved by Fritzing 1.0.4)
circuit board: 5.51927cm x 4.5cm
breadboards: 1

parts:
  Arduino_Nano_ESP32 = Arduino Nano ESP32
  BNO055 = Adafruit BNO055 STEMMA QT [part_number="Adafruit #4646"]
  PowerBoost_500C = PowerBoost 500 Charger
  S1 = Toggle Switch [package=THT]

nets:
  N1: Arduino_Nano_ESP32.Pin_2, BNO055.3.3V
  N2: Arduino_Nano_ESP32.Pin_8, BNO055.SDA
  N3: Arduino_Nano_ESP32.Pin_9, BNO055.SCL
  GND: Arduino_Nano_ESP32.Pin_14, Arduino_Nano_ESP32.Pin_19, BNO055.GND, PowerBoost_500C.GND, S1.L2
  N4: Arduino_Nano_ESP32.Pin_15, PowerBoost_500C.5.0V
  N5: PowerBoost_500C.ENABLE, S1.COM

notes:
  fall
  detector
  fall detector

custom parts:
  Arduino Nano ESP32: Arduino® Nano ESP32 tht.
  Adafruit BNO055 STEMMA QT: If you've ever ordered and wire up a 9-DOF sensor, chances are you've also realized the challenge of turning the sensor data from an accelerometer, gyroscope, and magnetometer into actual "3D space orientation"! Orientation is a hard problem to solve. The sensor fusion algorithms (the secret sauce that blends accelerometer, magnetometer, and gyroscope data into stable three-axis orientation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
  PowerBoost 500 Charger: The PowerBoost 500C is a little DC/DC boost converter module that can be powered by any 3.7V LiIon/LiPoly battery, and convert the battery output to 5.2V DC for running your 5V projects. At its heart is a TPS61090 boost converter from TI. This boost converter chip has some really nice extras such as low battery detection, 2A internal switch, synchronous conversion, excellent efficiency, and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
